// Logisim project Лаб5.circ as structural Verilog: 1 circuit, main circuit main
module main (
  input  D,
  input  C,
  input  in_3,
  input  T,
  input  C_2,
  input  J,
  input  C_3,
  input  K,
  output Q,
  output minus_Q,
  output Q_2,
  output minus_Q_2,
  output Q_3,
  output minus_Q_3
);

  wire nand_1_out, nand_2_out, nand_3_out, nand_4_out, nand_5_out, nand_6_out, nand_7_out, nand_8_out,
       nand_9_out, nand_14_out, nand_15_out;

  nand nand_1 (nand_1_out, T, C_2);
  nand nand_2 (nand_2_out, D, C);
  nand nand_3 (nand_3_out, nand_2_out, C);
  nand nand_4 (nand_4_out, minus_Q_3, J, C_3);
  nand nand_5 (nand_5_out, C_3, K, Q_3);
  nand nand_6 (nand_6_out, in_3, nand_1_out);
  nand nand_7 (nand_7_out, nand_6_out, nand_1_out);
  nand nand_8 (nand_8_out, nand_4_out, nand_9_out);
  nand nand_9 (nand_9_out, nand_8_out, nand_5_out);
  nand nand_10 (Q, nand_2_out, minus_Q);
  nand nand_11 (minus_Q, Q, nand_3_out);
  nand nand_12 (Q_2, nand_6_out, minus_Q_2);
  nand nand_13 (minus_Q_2, Q_2, nand_7_out);
  nand nand_14 (nand_14_out, nand_4_out, nand_8_out);
  nand nand_15 (nand_15_out, nand_9_out, nand_5_out);
  nand nand_16 (Q_3, nand_14_out, minus_Q_3);
  nand nand_17 (minus_Q_3, Q_3, nand_15_out);

  // Notes on the sheet:
  //   D-триггер
  //   T-триггер
  //   JK-триггер
endmodule
